# Fritzing sketch Schaltkreis (saved by Fritzing 0.4.3b)
breadboards: 1

parts:
  Pan = DC Motor
  Tilt = DC Motor
  Arduino = Arduino  # not connected
  Motor_Driver = L298  # not connected

nets:
  N1: Pan.pin_1, Tilt.pin_1
  N2: Pan.pin_2, Tilt.pin_2
